// Logisim project EP3.circ as structural Verilog: 7 circuits, main circuit main
module PC (
  input  [7:0] Input_Address,
  input  Set,
  input  Reset,
  input  Counter_UP,
  output [7:0] Output_Address
);

  wire and_1_out, and_2_out, and_3_out, and_4_out, and_5_out, and_6_out, and_7_out, and_8_out, and_9_out,
       and_10_out, and_11_out, and_12_out, and_13_out, and_14_out, and_15_out, and_16_out, j_k_ff_1_qn,
       j_k_ff_2_qn, j_k_ff_3_qn, j_k_ff_4_qn, j_k_ff_5_qn, j_k_ff_6_qn, j_k_ff_7_qn, or_1_out, or_2_out,
       or_3_out, or_4_out, or_5_out, or_6_out, or_7_out, or_8_out;

  and and_1 (and_1_out, Set, Input_Address[0]);
  J_K_Flip_Flop j_k_ff_1 (
    .J(1'b1), .clk(Counter_UP), .K(1'b1), .Q(Output_Address[0]), .Qn(j_k_ff_1_qn), .preset(and_1_out),
    .en(1'b1), .reset(or_2_out));
  and and_2 (and_2_out, Set, ~Input_Address[0]);  // AND_Gate
  and and_3 (and_3_out, Set, Input_Address[1]);
  or or_1 (or_1_out, Reset, and_6_out);
  or or_2 (or_2_out, Reset, and_2_out);
  J_K_Flip_Flop j_k_ff_2 (
    .J(1'b1), .clk(j_k_ff_1_qn), .K(1'b1), .Q(Output_Address[1]), .Qn(j_k_ff_2_qn), .preset(and_3_out),
    .en(1'b1), .reset(or_1_out));
  and and_4 (and_4_out, Set, Input_Address[2]);
  and and_5 (and_5_out, Set, ~Input_Address[2]);  // AND_Gate
  and and_6 (and_6_out, Set, ~Input_Address[1]);  // AND_Gate
  or or_3 (or_3_out, Reset, and_5_out);
  and and_7 (and_7_out, Set, Input_Address[3]);
  and and_8 (and_8_out, Set, ~Input_Address[3]);  // AND_Gate
  or or_4 (or_4_out, Reset, and_8_out);
  J_K_Flip_Flop j_k_ff_3 (
    .J(1'b1), .clk(j_k_ff_2_qn), .K(1'b1), .Q(Output_Address[2]), .Qn(j_k_ff_3_qn), .preset(and_4_out),
    .en(1'b1), .reset(or_3_out));
  and and_9 (and_9_out, Set, Input_Address[4]);
  and and_10 (and_10_out, Set, ~Input_Address[4]);  // AND_Gate
  or or_5 (or_5_out, Reset, and_10_out);
  J_K_Flip_Flop j_k_ff_4 (
    .J(1'b1), .clk(j_k_ff_3_qn), .K(1'b1), .Q(Output_Address[3]), .Qn(j_k_ff_4_qn), .preset(and_7_out),
    .en(1'b1), .reset(or_4_out));
  and and_11 (and_11_out, Set, Input_Address[5]);
  and and_12 (and_12_out, Set, ~Input_Address[5]);  // AND_Gate
  or or_6 (or_6_out, Reset, and_12_out);
  J_K_Flip_Flop j_k_ff_5 (
    .J(1'b1), .clk(j_k_ff_4_qn), .K(1'b1), .Q(Output_Address[4]), .Qn(j_k_ff_5_qn), .preset(and_9_out),
    .en(1'b1), .reset(or_5_out));
  and and_13 (and_13_out, Set, Input_Address[6]);
  and and_14 (and_14_out, Set, ~Input_Address[6]);  // AND_Gate
  and and_15 (and_15_out, Set, Input_Address[7]);
  or or_7 (or_7_out, Reset, and_14_out);
  J_K_Flip_Flop j_k_ff_6 (
    .J(1'b1), .clk(j_k_ff_5_qn), .K(1'b1), .Q(Output_Address[5]), .Qn(j_k_ff_6_qn), .preset(and_11_out),
    .en(1'b1), .reset(or_6_out));
  and and_16 (and_16_out, Set, ~Input_Address[7]);  // AND_Gate
  or or_8 (or_8_out, Reset, and_16_out);
  J_K_Flip_Flop j_k_ff_7 (
    .J(1'b1), .clk(j_k_ff_6_qn), .K(1'b1), .Q(Output_Address[6]), .Qn(j_k_ff_7_qn), .preset(and_13_out),
    .en(1'b1), .reset(or_7_out));
  J_K_Flip_Flop j_k_ff_8 (
    .J(1'b1), .clk(j_k_ff_7_qn), .K(1'b1), .Q(Output_Address[7]), .preset(and_15_out), .en(1'b1),
    .reset(or_8_out));  // open: Qn
endmodule

module CTRL (
  input  Entradas,
  input  in_2,
  input  [15:0] IR_OUT,
  input  [7:0] in_4,
  input  [15:0] ACC_OUT,
  input  [6:0] CHAR,
  output RAM_CLOCK,
  output RAM_LD,
  output CU,
  output PRN_EN,
  output IR_EN,
  output ACC_EN,
  output KEY_CLOCK,
  output PC_SET,
  output [7:0] PC_IN,
  output KEY_CLEAR,
  output [7:0] RAM_ADDRESS,
  output READING,
  output [2:0] S,
  output out_20,
  output OP,
  output [15:0] INPUT,
  output [15:0] OUT
);

  wire ADD, and_8_out, and_9_out, and_10_out, cmp_3_out_4, cmp_4_out_4, cmp_5_out_4, cmp_6_out_4,
       cmp_7_out_4, cmp_8_out_4, comparator_1_gt, comparator_2_eq, comparator_3_gt, comparator_4_eq,
       comparator_5_lt, comparator_6_lt, DIV, ENABLE, JDZ, JEQ, JGE, JGT, JLE, JLT, JMP, LDA, MUL, NOP,
       not_2_out, not_3_out, not_4_out, not_5_out, not_6_out, not_7_out, not_8_out, not_9_out, not_10_out,
       not_11_out, not_12_out, or_2_out, or_3_out, REM, STA, STOP, SUB, transistor_9_out, WAIT;
  wire [1:0] counter_1_q;

  CMP cmp_1 (.in_1(IR_OUT[7:0]), .in_2(8'hb), .out_4(LDA), .Enable(ENABLE));
  CMP cmp_2 (.in_1(IR_OUT[7:0]), .in_2(8'h32), .out_4(NOP), .Enable(ENABLE));
  CMP cmp_3 (.in_1(IR_OUT[7:0]), .in_2(8'h34), .out_4(cmp_3_out_4), .Enable(ENABLE));
  CMP cmp_4 (.in_1(IR_OUT[7:0]), .in_2(8'h35), .out_4(cmp_4_out_4), .Enable(ENABLE));
  CMP cmp_5 (.in_1(IR_OUT[7:0]), .in_2(8'h36), .out_4(cmp_5_out_4), .Enable(ENABLE));
  CMP cmp_6 (.in_1(IR_OUT[7:0]), .in_2(8'h37), .out_4(cmp_6_out_4), .Enable(ENABLE));
  CMP cmp_7 (.in_1(IR_OUT[7:0]), .in_2(8'h38), .out_4(cmp_7_out_4), .Enable(ENABLE));
  CMP cmp_8 (.in_1(IR_OUT[7:0]), .in_2(8'h39), .out_4(cmp_8_out_4), .Enable(ENABLE));
  CMP cmp_9 (.in_1(IR_OUT[7:0]), .in_2(8'h33), .out_4(JMP), .Enable(ENABLE));
  Comparator #(.width(16)) comparator_1 (.a(ACC_OUT), .b({16{1'b0}}), .gt(comparator_1_gt));  // open: eq, lt
  Comparator #(.width(16)) comparator_2 (.a(ACC_OUT), .b({16{1'b0}}), .eq(comparator_2_eq));  // open: gt, lt
  Comparator #(.width(16)) comparator_3 (.a(ACC_OUT), .b({16{1'b0}}), .gt(comparator_3_gt));  // open: eq, lt
  Comparator #(.width(16)) comparator_4 (.a(ACC_OUT), .b({16{1'b0}}), .eq(comparator_4_eq));  // open: gt, lt
  Comparator #(.width(16)) comparator_5 (.a(ACC_OUT), .b({16{1'b0}}), .lt(comparator_5_lt));  // open: gt, eq
  Comparator #(.width(16)) comparator_6 (.a(ACC_OUT), .b({16{1'b0}}), .lt(comparator_6_lt));  // open: gt, eq
  CMP cmp_10 (.in_1(IR_OUT[7:0]), .in_2(8'hc), .out_4(STA), .Enable(ENABLE));
  CMP cmp_11 (.in_1(IR_OUT[7:0]), .in_2(8'h46), .out_4(STOP), .Enable(ENABLE));
  and and_1 (JLE, cmp_3_out_4, ~comparator_1_gt);  // AND_Gate
  and and_2 (JDZ, cmp_4_out_4, ~comparator_2_eq);  // AND_Gate
  and and_3 (JGT, cmp_5_out_4, comparator_3_gt);
  and and_4 (JEQ, cmp_6_out_4, comparator_4_eq);
  and and_5 (JLT, cmp_7_out_4, comparator_5_lt);
  and and_6 (JGE, cmp_8_out_4, ~comparator_6_lt);  // AND_Gate
  or or_1 (ACC_EN, LDA, OP);
  CMP cmp_12 (.in_1(IR_OUT[7:0]), .in_2(8'h15), .out_4(ADD), .Enable(ENABLE));
  CMP cmp_13 (.in_1(IR_OUT[7:0]), .in_2(8'h16), .out_4(SUB), .Enable(ENABLE));
  CMP cmp_14 (.in_1(IR_OUT[7:0]), .in_2(8'h17), .out_4(MUL), .Enable(ENABLE));
  CMP cmp_15 (.in_1(IR_OUT[7:0]), .in_2(8'h18), .out_4(DIV), .Enable(ENABLE));
  CMP cmp_16 (.in_1(IR_OUT[7:0]), .in_2(8'h19), .out_4(REM), .Enable(ENABLE));
  Transistor #(.\type ("n"), .width(3)) transistor_1 (.in(3'b000), .out(S), .gate(ADD));
  Transistor #(.\type ("n"), .width(3)) transistor_2 (.in(3'b001), .out(S), .gate(SUB));
  Transistor #(.\type ("n"), .width(3)) transistor_3 (.in(3'b010), .out(S), .gate(MUL));
  Transistor #(.\type ("n"), .width(3)) transistor_4 (.in(3'b011), .out(S), .gate(DIV));
  Transistor #(.\type ("n"), .width(3)) transistor_5 (.in(3'b100), .out(S), .gate(REM));
  CMP cmp_17 (.in_1(IR_OUT[7:0]), .in_2(8'h1f), .out_4(out_20), .Enable(ENABLE));
  nor nor_1 (RAM_LD, STA, out_20);
  and and_7 (KEY_CLEAR, ~WAIT, out_20);  // AND_Gate
  Key_interpreter key_interpreter_1 (
    .Clock_out(KEY_CLOCK), .Start(out_20), .Reset(in_2), .Output(INPUT), .Clock(Entradas), .char(CHAR),
    .Lendo(WAIT));
  CMP cmp_18 (.in_1(IR_OUT[7:0]), .in_2(8'h29), .out_4(PRN_EN), .Enable(ENABLE));
  Demultiplexer #(.select(2), .enable("false")) demultiplexer_1 (
    .out0(IR_EN), .out1(CU), .out2(ENABLE), .in(1'b1), .sel(counter_1_q));  // open: out3
  Counter #(.width(2), .max('h2)) counter_1 (
    .Q(counter_1_q), .clk(and_8_out), .clr(in_2));  // open: load, D, count, carry
  and and_8 (and_8_out, ~STOP, ~WAIT, Entradas);  // AND_Gate
  and and_9 (and_9_out, ~WAIT, out_20);  // AND_Gate
  or or_2 (or_2_out, LDA, STA, PRN_EN, and_9_out, OP);
  Transistor #(.width(8)) transistor_6 (.in(in_4), .out(RAM_ADDRESS), .gate(or_2_out));
  and and_10 (and_10_out, ~WAIT, out_20);  // AND_Gate
  or or_3 (or_3_out, and_10_out, STA);
  or or_4 (PC_SET, JMP, JLE, JDZ, JGT, JEQ, JLT, JGE);
  or or_5 (OP, ADD, SUB, MUL, DIV, REM);
  Transistor #(.\type ("n"), .width(8)) transistor_7 (.in(IR_OUT[15:8]), .out(RAM_ADDRESS), .gate(or_2_out));
  Transistor #(.gate("br")) transistor_8 (.in(Entradas), .out(RAM_CLOCK), .gate(or_3_out));
  not not_1 (RAM_CLOCK, not_2_out);
  not not_2 (not_2_out, not_7_out);
  not not_3 (not_3_out, not_5_out);
  not not_4 (not_4_out, not_10_out);
  not not_5 (not_5_out, not_4_out);
  not not_6 (not_6_out, transistor_9_out);
  Transistor #(.\type ("n")) transistor_9 (.in(Entradas), .out(transistor_9_out), .gate(or_3_out));
  not not_7 (not_7_out, not_8_out);
  not not_8 (not_8_out, not_9_out);
  not not_9 (not_9_out, not_3_out);
  not not_10 (not_10_out, not_12_out);
  not not_11 (not_11_out, not_6_out);
  not not_12 (not_12_out, not_11_out);

  assign PC_IN = IR_OUT[15:8];
  assign READING = out_20;

  // Other names for the same wires on the sheet: CLOCK = Entradas; INN = out_20; COD[7:0] = IR_OUT[7:0];
  //   IR_ADDR[7:0] = IR_OUT[15:8]; JUMP = PC_SET; MATH = OP; OUTPUT[15:0] = OUT; PC_OUT[7:0] = in_4; PRN = PRN_EN;
  //   RESET = in_2

  // Notes on the sheet:
  //   LDA - 11
  //   NOP - 50
  //   Jumps
  //   JMP - 51
  //   JLE - 52
  //   JDZ - 53
  //   JGT - 54
  //   JEQ - 55
  //   JLT - 56
  //   JGE - 57
  //   Instruções
  //   STA - 12
  //   STP - 70
  //   Aritimética
  //   ADD - 21
  //   SUB - 22
  //   MUL - 23
  //   DIV - 24
  //   REM - 25
  //   Saídas
  //   INN - 31
  //   PRN - 41
  //   Ciclo de Instrução
  //   JMP - PC_SET
  //   É operação
  //   Selecionar acesso à RAM
  //   Clock pra RAM
endmodule

module CMP (
  input  [7:0] in_1,
  input  [7:0] in_2,
  input  Enable,
  output out_4
);

  wire and_1_out;
  wire [7:0] xnor_1_out;

  assign xnor_1_out = ~(in_1 ^ in_2);  // XNOR_Gate xnor_1, 8 bits wide
  and and_1 (and_1_out, xnor_1_out[0], xnor_1_out[1], xnor_1_out[2], xnor_1_out[3], xnor_1_out[4], xnor_1_out[5], xnor_1_out[6], xnor_1_out[7]);
  and and_2 (out_4, and_1_out, Enable);
endmodule

module main (
  input  [2:0] in_1,
  output [7:0] out_2,
  output [15:0] out_3,
  output [15:0] out_4,
  output [6:0] out_5,
  output [7:0] out_6,
  output [15:0] out_7,
  output [15:0] out_8,
  output [15:0] out_9
);

  wire ACC_EN, CLOCK, clock_2_out, CU, IR_EN, KEY_CLEAR, KEY_CLOCK, key_interpreter_1_clock_out,
       key_interpreter_1_lendo, OP, PC_SET, PRN_EN, RAM_CLOCK, RAM_LOAD, READING, RESET, Reset_out, SCAN,
       Start_out;
  wire [2:0] S;
  wire [6:0] CHAR;
  wire [7:0] RAM_ADDR;
  wire [15:0] INPUT, IR_OUT, OUT, Output_q, ram_1_data, transistor_2_out, transistor_5_out;

  Button button_1 (.out(RESET));
  Clock clock_1 (.out(CLOCK));
  Register #(.width(16)) Output (.D(out_9), .en(PRN_EN), .Q(Output_q), .clk(CLOCK), .clr(RESET));
  RAM #(.dataWidth(16)) ram_1 (
    .addr(RAM_ADDR), .data(ram_1_data), .sel(1'b1), .clk(RAM_CLOCK), .ld(RAM_LOAD));  // open: clr
  Hex_Digit_Display hex_digit_display_1 (.value(Output_q[15:12]));  // open: dp
  Hex_Digit_Display hex_digit_display_2 (.value(Output_q[11:8]));  // open: dp
  CTRL ctrl_1 (
    .IR_OUT(IR_OUT), .RAM_LD(RAM_LOAD), .IR_EN(IR_EN), .CU(CU), .RAM_CLOCK(RAM_CLOCK), .Entradas(CLOCK),
    .in_2(RESET), .PC_IN(out_2), .PC_SET(PC_SET), .RAM_ADDRESS(RAM_ADDR), .in_4(out_6), .ACC_EN(ACC_EN),
    .ACC_OUT(out_3), .S(S), .OP(OP), .OUT(OUT), .out_20(SCAN), .PRN_EN(PRN_EN), .CHAR(CHAR),
    .KEY_CLOCK(KEY_CLOCK), .KEY_CLEAR(KEY_CLEAR), .READING(READING), .INPUT(INPUT));
  Transistor #(.width(16)) transistor_1 (.in(transistor_2_out), .out(ram_1_data), .gate(RAM_LOAD));
  Transistor #(.gate("br"), .width(16)) transistor_2 (.in(out_3), .out(transistor_2_out), .gate(SCAN));
  Transistor #(.\type ("n"), .width(16)) transistor_3 (.in(INPUT), .out(transistor_2_out), .gate(SCAN));
  Transistor #(.\type ("n"), .gate("br"), .width(16)) transistor_4 (.in(ram_1_data), .out(out_9), .gate(RAM_LOAD));
  Hex_Digit_Display hex_digit_display_3 (.value(Output_q[3:0]));  // open: dp
  Hex_Digit_Display hex_digit_display_4 (.value(Output_q[7:4]));  // open: dp
  Keyboard keyboard_1 (.clk(KEY_CLOCK), .re(READING), .clr(KEY_CLEAR), .data(CHAR));  // open: avail
  Hex_Digit_Display hex_digit_display_5 (.value(INPUT[11:8]));  // open: dp
  Hex_Digit_Display hex_digit_display_6 (.value(INPUT[15:12]));  // open: dp
  Hex_Digit_Display hex_digit_display_7 (.value(INPUT[7:4]));  // open: dp
  Hex_Digit_Display hex_digit_display_8 (.value(INPUT[3:0]));  // open: dp
  Transistor #(.width(16)) transistor_5 (.in(out_9), .out(transistor_5_out), .gate(OP));
  Transistor #(.\type ("n"), .width(16)) transistor_6 (.in(out_7), .out(transistor_5_out), .gate(OP));
  Register #(.width(16)) ACC (.D(transistor_5_out), .en(ACC_EN), .Q(out_3), .clk(CLOCK), .clr(RESET));
  PC pc_1 (.Set(PC_SET), .Reset(RESET), .Counter_UP(CU), .Input_Address(out_2), .Output_Address(out_6));
  Transistor #(.\type ("n"), .width(16)) transistor_7 (.in(out_3), .out(out_8), .gate(RAM_LOAD));
  Register #(.width(16)) IR (.D(out_9), .en(IR_EN), .Q(IR_OUT), .clk(CLOCK), .clr(RESET));
  Clock clock_2 (.out(clock_2_out));
  Key_interpreter key_interpreter_1 (
    .Clock_out(key_interpreter_1_clock_out), .Start(Start_out), .Reset(Reset_out), .Output(out_4),
    .Clock(clock_2_out), .char(out_5), .Lendo(key_interpreter_1_lendo));
  Button u_Reset (.out(Reset_out));
  Button Start (.out(Start_out));
  ALU alu_1 (.A(out_8), .B(out_9), .S(in_1), .out_4(out_7));  // open: Overflow, div_0
  Keyboard keyboard_2 (
    .clk(key_interpreter_1_clock_out), .re(key_interpreter_1_lendo), .clr(Start_out), .data(out_5));  // open: avail

  // Other names for the same wires on the sheet: ACC_OUT[15:0] = out_3; ALU_OUT[15:0] = out_7; PC_IN[7:0] = out_2;
  //   PC_OUT[7:0] = out_6; RAM_OUT[15:0] = out_9

  // Notes on the sheet:
  //   Início
  //   RAM
endmodule

module CMP16 (
  input  [15:0] in_1,
  input  [15:0] in_2,
  output out_3,
  output out_4,
  output out_5
);

  wire [14:0] sub_1_resultado;
  wire [15:0] xnor_1_out;

  assign xnor_1_out = ~(in_1 ^ in_2);  // XNOR_Gate xnor_1, 16 bits wide
  Sub sub_1 (.Minuendo(in_1), .Subtraendo(in_2), .Resultado({out_5, sub_1_resultado}));  // open: Overflow
  and and_1 (out_3, xnor_1_out[0], xnor_1_out[1], xnor_1_out[2], xnor_1_out[3], xnor_1_out[4], xnor_1_out[5], xnor_1_out[6], xnor_1_out[7], xnor_1_out[8], xnor_1_out[9], xnor_1_out[10], xnor_1_out[11], xnor_1_out[12], xnor_1_out[13], xnor_1_out[14], xnor_1_out[15]);
  nor nor_1 (out_4, out_3, out_5);
endmodule

module Key_interpreter (
  input  Reset,
  input  Start,
  input  Clock,
  input  [6:0] char,
  output Clock_out,
  output Lendo,
  output [15:0] Output
);

  wire comparator_1_eq, comparator_2_lt, comparator_3_gt, comparator_4_lt, comparator_5_gt, comparator_6_lt,
       comparator_7_gt, ENABLE, fim, MAI, MIN, NUM, or_3_out, RESET_t;
  wire [6:0] IN, subtractor_1_out, subtractor_2_out, subtractor_3_out;

  and and_1 (Clock_out, Lendo, Clock);
  Comparator #(.width(7)) comparator_1 (.a(char), .b(7'b0001010), .eq(comparator_1_eq));  // open: gt, lt
  Comparator #(.width(7)) comparator_2 (.a(char), .b(7'b0110000), .lt(comparator_2_lt));  // open: gt, eq
  Comparator #(.width(7)) comparator_3 (.a(char), .b(7'b0111001), .gt(comparator_3_gt));  // open: eq, lt
  Comparator #(.width(7)) comparator_4 (.a(char), .b(7'b1100001), .lt(comparator_4_lt));  // open: gt, eq
  Comparator #(.width(7)) comparator_5 (.a(char), .b(7'b1100110), .gt(comparator_5_gt));  // open: eq, lt
  Comparator #(.width(7)) comparator_6 (.a(char), .b(7'b1000001), .lt(comparator_6_lt));  // open: gt, eq
  Comparator #(.width(7)) comparator_7 (.a(char), .b(7'b1000110), .gt(comparator_7_gt));  // open: eq, lt
  or or_1 (RESET_t, Reset, Start);
  or or_2 (fim, comparator_1_eq, Reset);
  nor nor_1 (NUM, comparator_2_lt, comparator_3_gt);
  Subtractor #(.width(7)) subtractor_1 (.a(char), .b(7'b0110000), .out(subtractor_1_out));  // open: bin, bout
  nor nor_2 (MIN, comparator_4_lt, comparator_5_gt);
  nor nor_3 (MAI, comparator_6_lt, comparator_7_gt);
  Transistor #(.\type ("n"), .width(7)) transistor_1 (.in(subtractor_1_out), .out(IN), .gate(NUM));
  Transistor #(.\type ("n"), .width(7)) transistor_2 (.in(subtractor_2_out), .out(IN), .gate(MIN));
  Subtractor #(.width(7)) subtractor_2 (.a(char), .b(7'b1010111), .out(subtractor_2_out));  // open: bin, bout
  Subtractor #(.width(7)) subtractor_3 (.a(char), .b(7'b0110111), .out(subtractor_3_out));  // open: bin, bout
  Transistor #(.\type ("n"), .width(7)) transistor_3 (.in(subtractor_3_out), .out(IN), .gate(MAI));
  D_Flip_Flop d_ff_1 (.Q(Lendo), .preset(Start), .reset(fim));  // open: clk, D, Qn, en
  or or_3 (or_3_out, NUM, MIN, MAI);
  and and_2 (ENABLE, or_3_out, Clock_out);
  D_Flip_Flop d_ff_2 (.clk(ENABLE), .D(IN[0]), .Q(Output[0]), .reset(RESET_t));  // open: Qn, preset, en
  D_Flip_Flop d_ff_3 (.clk(ENABLE), .D(IN[1]), .Q(Output[1]), .reset(RESET_t));  // open: Qn, preset, en
  D_Flip_Flop d_ff_4 (.clk(ENABLE), .D(IN[2]), .Q(Output[2]), .reset(RESET_t));  // open: Qn, preset, en
  D_Flip_Flop d_ff_5 (.clk(ENABLE), .D(IN[3]), .Q(Output[3]), .reset(RESET_t));  // open: Qn, preset, en
  D_Flip_Flop d_ff_6 (.clk(ENABLE), .D(Output[0]), .Q(Output[4]), .reset(RESET_t));  // open: Qn, preset, en
  D_Flip_Flop d_ff_7 (.clk(ENABLE), .D(Output[1]), .Q(Output[5]), .reset(RESET_t));  // open: Qn, preset, en
  D_Flip_Flop d_ff_8 (.clk(ENABLE), .D(Output[2]), .Q(Output[6]), .reset(RESET_t));  // open: Qn, preset, en
  D_Flip_Flop d_ff_9 (.clk(ENABLE), .D(Output[3]), .Q(Output[7]), .reset(RESET_t));  // open: Qn, preset, en
  D_Flip_Flop d_ff_10 (.clk(ENABLE), .D(Output[8]), .Q(Output[12]), .reset(RESET_t));  // open: Qn, preset, en
  D_Flip_Flop d_ff_11 (.clk(ENABLE), .D(Output[4]), .Q(Output[8]), .reset(RESET_t));  // open: Qn, preset, en
  D_Flip_Flop d_ff_12 (.clk(ENABLE), .D(Output[9]), .Q(Output[13]), .reset(RESET_t));  // open: Qn, preset, en
  D_Flip_Flop d_ff_13 (.clk(ENABLE), .D(Output[5]), .Q(Output[9]), .reset(RESET_t));  // open: Qn, preset, en
  D_Flip_Flop d_ff_14 (.clk(ENABLE), .D(Output[10]), .Q(Output[14]), .reset(RESET_t));  // open: Qn, preset, en
  D_Flip_Flop d_ff_15 (.clk(ENABLE), .D(Output[6]), .Q(Output[10]), .reset(RESET_t));  // open: Qn, preset, en
  D_Flip_Flop d_ff_16 (.clk(ENABLE), .D(Output[11]), .Q(Output[15]), .reset(RESET_t));  // open: Qn, preset, en
  D_Flip_Flop d_ff_17 (.clk(ENABLE), .D(Output[7]), .Q(Output[11]), .reset(RESET_t));  // open: Qn, preset, en
  Hex_Digit_Display hex_digit_display_1 (.value(Output[15:12]));  // open: dp
  Hex_Digit_Display hex_digit_display_2 (.value(Output[11:8]));  // open: dp
  Hex_Digit_Display hex_digit_display_3 (.value(Output[7:4]));  // open: dp
  Hex_Digit_Display hex_digit_display_4 (.value(Output[3:0]));  // open: dp

  // Other names for the same wires on the sheet: CLK_OUT = Clock_out; RES = Reset

  // Notes on the sheet:
  //   Enter
  //   0 - 9
  //   a - f
  //   A - F
endmodule

module teste (
  input  in_1
);

  wire and_1_out, not_1_out, t_ff_1_q;

  not not_1 (not_1_out, in_1);
  and and_1 (and_1_out, in_1, not_1_out);
  T_Flip_Flop t_ff_1 (.clk(and_1_out), .T(1'b1), .Q(t_ff_1_q));  // open: Qn, preset, reset, en
endmodule
